# Fritzing sketch circuit (saved by Fritzing 0.9.2b)
breadboards: 1

parts:
  Componente1 = Arduino Nano (Rev3.0)
  R1 = Resistor [tolerance=±5% resistance=1k package=THT]
  R3 = Resistor [tolerance=±5% resistance=1k package=THT]
  R4 = Resistor [tolerance=±5% resistance=1k package=THT]
  R5 = Resistor [tolerance=±5% resistance=1k package=THT]
  R8 = Resistor [tolerance=±5% resistance=1k package=THT]
  T1 = LM35 Temperature Sensor [package="TO92 [THT]"]

nets:
  GND: Componente1.GND, R8.Pin_1, T1.GND
  N1: Componente1.5V, R1.Pin_0
  N2: Componente1.A0, T1.Vout
  N3: R1.Pin_1, R3.Pin_0
  N4: R3.Pin_1, R4.Pin_0
  N5: R4.Pin_1, R5.Pin_0
  N6: R5.Pin_1, R8.Pin_0, T1.+Vs
